# Fritzing sketch Serious_Toys (saved by Fritzing 0.9.3b)

parts:
  Part1 = Arduino Micro (Rev3)
  Grove1 = Grove 3 Axis Digital Accelerometer 16g
  Part2 = PowerBoost 1000 Basic
  Part3 = TFT 1.8 inch 160x128 w microSD [part_number=358]
  U1 = LIPO-110mAh [package=lipo-110]

nets:
  N1: Part1.MOSI, Part3.MOSI
  GND: Part1.GND, Grove1.GND, Part2.GND, Part3.GND, U1.-
  N2: Part1.D2/SDA, Grove1.SCL
  N3: Part1.D3/SCL, Grove1.SDA
  N4: Part1.D4_PWM/A6, Part3.TFTCS
  N5: Part1.D5_PWM, Part3.TFTDC
  N6: Part1.D6_PWM/A7, Part3.RESET
  N7: Part1.SCK, Part3.SCLK
  N8: Part1.VIN, Part2.5.0V
  5V: Part1.5V, Grove1.VCC, Part3.+5V
  N9: Part2.VBAT, U1.+

custom parts:
  PowerBoost 1000 Basic: The PowerBoost 1000 is a little DC/DC boost converter module that can run from 1.8V batteries or higher, and convert the battery output to 5.2V DC for running your 5V projects. At its heart is a TPS61030 boost converter from TI. This boost converter chip has some really nice extras such as low battery detection, 4A internal switch, synchronous conversion, excellent efficiency, and 700KHz high-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
  TFT 1.8 inch 160x128 w microSD: This lovely little display breakout is the best way to add a small, colorful and bright display to any project. Since the display uses 4-wire SPI to communicate and has its own pixel-addressable frame buffer, it can be used with every kind of microcontroller. Even a very small one with low memory and few pins available! The 1.8" display has 128x160 color pixels.

// code stored in the sketch: Schematics.ino
/*

 TFT Pong

 This example for the Arduino screen reads the values
 of 2 potentiometers to move a rectangular platform
 on the x and y axes. The platform can intersect
 with a ball causing it to bounce.

 This example code is in the public domain.

 Created by Tom Igoe December 2012
 Modified 15 April 2013 by Scott Fitzgerald

 http://www.arduino.cc/en/Tutorial/TFTPong

 */

#include <TFT.h>  // Arduino LCD library
#include <SPI.h>

// pin definition for the Uno
#define cs   4
#define dc   5
#define rst  6

// pin definition for the Leonardo
// #define cs   7
// #define dc   0
// #define rst  1

TFT TFTscreen = TFT(cs, dc, rst);

// variables for the position of the ball and paddle
int paddleX = 0;
int paddleY = 0;
int oldPaddleX, oldPaddleY;
int ballDirectionX = 1;
int ballDirectionY = 1;

int ballSpeed = 10; // lower numbers are faster

int ballX, ballY, oldBallX, oldBallY;

void setup() {
  // initialize the display
  TFTscreen.begin();
  // black background
  TFTscreen.background(0, 0, 0);
}

void loop() {

  // save the width and height of the screen
  int myWidth = TFTscreen.width();
  int myHeight = TFTscreen.height();

  // map the paddle's location to the position of the potentiometers
  paddleX = map(analogRead(A0), 512, -512, 0, myWidth) - 20 / 2;
  paddleY = map(analogRead(A1), 512, -512, 0, myHeight) - 5 / 2;

  // set the fill color to black and erase the previous
  // position of the paddle if different from present
  TFTscreen.fill(0, 0, 0);

  if (oldPaddleX != paddleX || oldPaddleY != paddleY) {
    TFTscreen.rect(oldPaddleX, oldPaddleY, 20, 5);
  }

  // draw the paddle on screen, save the current position
  // as the previous.
  TFTscreen.fill(255, 255, 255);

  TFTscreen.rect(paddleX, paddleY, 20, 5);
  oldPaddleX = paddleX;
  oldPaddleY = paddleY;

  // update the ball's position and draw it on screen
  if (millis() % ballSpeed < 2) {
    moveBall();
  }
}

// this function determines the ball's position on screen
void moveBall() {
  // if the ball goes offscreen, reverse the direction:
  if (ballX > TFTscreen.width() || ballX < 0) {
    ballDirectionX = -ballDirectionX;
  }

  if (ballY > TFTscreen.height() || ballY < 0) {
    ballDirectionY = -ballDirectionY;
  }

  // check if the ball and the paddle occupy the same space on screen
  if (inPaddle(ballX, ballY, paddleX, paddleY, 20, 5)) {
    ballDirectionX = -ballDirectionX;
    ballDirectionY = -ballDirectionY;
  }

  // update the ball's position
  ballX += ballDirectionX;
  ballY += ballDirectionY;

  // erase the ball's previous position
  TFTscreen.fill(0, 0, 0);

  if (oldBallX != ballX || oldBallY != ballY) {
    TFTscreen.rect(oldBallX, oldBallY, 5, 5);
  }


  // draw the ball's current position
  TFTscreen.fill(255, 255, 255);
  TFTscreen.rect(ballX, ballY, 5, 5);

  oldBallX = ballX;
  oldBallY = ballY;

}

// this function checks the position of the ball
// to see if it intersects with the paddle
boolean inPaddle(int x, int y, int rectX, int rectY, int rectWidth, int rectHeight) {
  boolean result = false;

  if ((x >= rectX && x <= (rectX + rectWidth)) &&
      (y >= rectY && y <= (rectY + rectHeight))) {
    result = true;
  }

  return result;
}
